# Fritzing sketch ArduinoUNO_LCD_I2C_DS3231_button (saved by Fritzing 0.9.2b)
breadboards: 1

parts:
  Part1 = Arduino Uno (Rev3)
  LCD1 = LCD screen  # not connected
  R2 = Resistor [tolerance=±5% resistance=10k package=THT]
  R3 = Resistor [tolerance=±5% resistance=10k package=THT]
  S1 = Pushbutton [package="[THT]"]
  S2 = Pushbutton [package="[THT]"]
  S3 = Pushbutton [package="[THT]"]
  Q1 = NPN-Transistor [package="TO92 [THT]"]
  R4 = Resistor [tolerance=±5% resistance=10k package=THT]
  J1 = Piezo Speaker
  S4 = Pushbutton [package="[THT]"]
  ZS-042_RTC1 = ZS-042 RTC Module

nets:
  N1: Part1.A4/SDA, R2.Pin_0, ZS-042_RTC1.SDA
  N2: Part1.A5/SCL, R3.Pin_0, ZS-042_RTC1.SCL
  N3: Part1.D8, S1.Pin_3, S1.Pin_4
  N4: Part1.D10_PWM/SS, R4.Pin_0
  GND: Part1.GND, S1.Pin_1, S1.Pin_2, S2.Pin_1, S2.Pin_2, S3.Pin_1, S3.Pin_2, S4.Pin_1, S4.Pin_2, ZS-042_RTC1.GND
  N5: Part1.D2, ZS-042_RTC1.SQW
  N6: Part1.D4, S4.Pin_3, S4.Pin_4
  N7: Part1.D5_PWM, S3.Pin_3, S3.Pin_4
  N8: Part1.D6_PWM, S2.Pin_3, S2.Pin_4
  5V: Part1.5V, R2.Pin_1, R3.Pin_1, ZS-042_RTC1.VCC
  N9: Q1.B, R4.Pin_1
  N10: Q1.C, J1.pin2
